# Fritzing sketch Circuit sketch (saved by Fritzing 0.9.3b)

parts:
  Mod1 = Raspberry Pi Pico
  DS1 = DS18B20 1-Wire Temperature Sensor Probe
  OLED1 = OLED 128x64 I2C Monochrome Display VDD-GND
  LED1 = LED - 5mm [color="Green (560nm)" package="5 mm [THT]"]
  R1 = Resistor [tolerance=±5% resistance=220 package="0603 [SMD]"]
  R2 = Resistor [tolerance=±5% resistance=4.7k package="0603 [SMD]"]

nets:
  N1: Mod1.pin_11, R2.Pin_1
  N2: Mod1.pin_21, OLED1.SDA
  N3: Mod1.pin_22, OLED1.SCK
  GND: Mod1.pin_28, Mod1.pin_38, Mod1.pin_42, DS1.GND, OLED1.GND, LED1.cathode
  N4: Mod1.pin_29, R1.Pin_0
  VDD: Mod1.pin_39, DS1.VDD, OLED1.VDD

notes:
  4.7k
  220

custom parts:
  Raspberry Pi Pico: Raspberry Pi Pico. Based around the RP2040 microcontroller the Pico is a low cost microcontroller device bringing Raspberry Pi quality, cost, and easy of use to the microcontroller space. Jan 2021, Split part in to two versions: tht (this one) and SMD. This one will drill holes for a .1 in header in pcb to allow plugging in the module as well as providing pads to solder the module to the top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
  OLED 128x64 I2C Monochrome Display VDD-GND: OLED 128x64 I2C Monochrome Display. Note: there are two variants of this part, this one is the VDD GND SCK SDA variant. The other is GND VDD SCK SDA. Make sure you select the part that matches your module as using the incorrect part will probably destroy your module! In addition the mounting holes are marked on silkscreen but not by default drilled. If you want drilled mounting holes, copy a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
